// Digital circuit ALU.dig as structural Verilog
module ALU (
  input  [31:0] A,
  input  [31:0] B,
  input  [4:0] ALU_Ctrl,
  output [31:0] Result,
  output Z,
  output N,
  output C,
  output V
);

  wire add_1_c_o, and_1_out, and_2_out, comparator_1_eq, nor_1_out, sub_1_c_o, xnor_1_out, xor_1_out,
       xor_2_out, xor_3_out;
  wire [1:0] multiplexer_8_out;
  wire [3:0] multiplexer_7_out;
  wire [4:0] nor_2_out;
  wire [5:0] bitcount_1_out, sub_2_s;
  wire [7:0] multiplexer_6_out;
  wire [15:0] multiplexer_1_out;
  wire [31:0] add_1_s, and_3_out, div_1_q, div_1_r, multiplexer_2_out, multiplexer_3_out, multiplexer_9_out,
       not_1_out, or_1_out, sub_1_s, xor_4_out;
  wire [63:0] mul_1_mul;

  Comparator #(.Bits(32)) comparator_1 (.a(B), .b({32{1'b0}}), .eq(comparator_1_eq));  // open: gt, lt
  Add #(.Bits(32)) add_1 (.a(A), .b(B), .c_i(1'b0), .s(add_1_s), .c_o(add_1_c_o));
  nor nor_1 (nor_1_out, A[15], A[0], A[1], A[2], A[3], A[4], A[5], A[6], A[7], A[8], A[9], A[10], A[11], A[12], A[13], A[14], A[16], A[17], A[18], A[19], A[20], A[21], A[22], A[23], A[24], A[25], A[26], A[27], A[28], A[29], A[30], A[31]);
  xnor xnor_1 (xnor_1_out, A[31], B[31]);
  xor xor_1 (xor_1_out, A[31], add_1_s[31]);
  xor xor_2 (xor_2_out, A[31], sub_1_s[31]);
  Sub #(.Bits(32)) sub_1 (.a(A), .b(B), .c_i(1'b0), .s(sub_1_s), .c_o(sub_1_c_o));
  Mul #(.Bits(32)) mul_1 (.a(A), .b(B), .mul(mul_1_mul));
  Div #(.Bits(32)) div_1 (.a(A), .b(B), .q(div_1_q), .r(div_1_r));
  and and_1 (and_1_out, xnor_1_out, xor_1_out);
  xor xor_3 (xor_3_out, A[31], B[31]);
  and and_2 (and_2_out, xor_3_out, xor_2_out);
  nor nor_2 (nor_2_out[4], A[0], A[1], A[2], A[3], A[4], A[5], A[6], A[7], A[8], A[9], A[10], A[11], A[12], A[13], A[14], A[15]);
  Multiplexer #(.Bits(16)) multiplexer_1 (.sel(nor_2_out[4]), .in_0(A[31:16]), .in_1(A[15:0]), .out(multiplexer_1_out));
  Multiplexer #(.Bits(32)) multiplexer_2 (
    .sel(comparator_1_eq), .in_0(div_1_q), .in_1({32{1'b1}}), .out(multiplexer_2_out));
  Multiplexer #(.Bits(32)) multiplexer_3 (.sel(comparator_1_eq), .in_0(div_1_r), .in_1(A), .out(multiplexer_3_out));
  assign and_3_out = A & B;  // And and_3, 32 bits wide
  Multiplexer #(.Selector_Bits(4)) multiplexer_4 (
    .sel(ALU_Ctrl[3:0]), .in_0(and_1_out), .in_1(and_2_out), .in_2(1'b0), .in_3(1'b0), .in_4(1'b0),
    .in_5(1'b0), .in_6(1'b0), .in_7(1'b0), .in_8(1'b0), .in_9(1'b0), .in_10(1'b0), .in_11(1'b0),
    .in_12(1'b0), .in_13(1'b0), .in_14(1'b0), .in_15(1'b0), .out(V));
  assign or_1_out = A | B;  // Or or_1, 32 bits wide
  Multiplexer #(.Selector_Bits(4)) multiplexer_5 (
    .sel(ALU_Ctrl[3:0]), .in_0(add_1_c_o), .in_1(sub_1_c_o), .in_2(1'b0), .in_3(1'b0), .in_4(1'b0),
    .in_5(1'b0), .in_6(1'b0), .in_7(1'b0), .in_8(1'b0), .in_9(1'b0), .in_10(1'b0), .in_11(1'b0),
    .in_12(1'b0), .in_13(1'b0), .in_14(1'b0), .in_15(1'b0), .out(C));
  assign xor_4_out = A ^ B;  // XOr xor_4, 32 bits wide
  assign not_1_out = ~A;  // Not not_1, 32 bits wide
  BitCount #(.Bits(32)) bitcount_1 (.in(A), .out(bitcount_1_out));
  nor nor_3 (nor_2_out[3], multiplexer_1_out[0], multiplexer_1_out[1], multiplexer_1_out[2], multiplexer_1_out[3], multiplexer_1_out[4], multiplexer_1_out[5], multiplexer_1_out[6], multiplexer_1_out[7]);
  Sub #(.Bits(6)) sub_2 (.a(6'b100000), .b(bitcount_1_out), .c_i(1'b0), .s(sub_2_s));  // open: c_o
  Multiplexer #(.Bits(8)) multiplexer_6 (
    .sel(nor_2_out[3]), .in_0(multiplexer_1_out[15:8]), .in_1(multiplexer_1_out[7:0]), .out(multiplexer_6_out));
  nor nor_4 (nor_2_out[2], multiplexer_6_out[0], multiplexer_6_out[1], multiplexer_6_out[2], multiplexer_6_out[3]);
  Multiplexer #(.Bits(4)) multiplexer_7 (
    .sel(nor_2_out[2]), .in_0(multiplexer_6_out[7:4]), .in_1(multiplexer_6_out[3:0]), .out(multiplexer_7_out));
  nor nor_5 (nor_2_out[1], multiplexer_7_out[0], multiplexer_7_out[1]);
  Multiplexer #(.Bits(2)) multiplexer_8 (
    .sel(nor_2_out[1]), .in_0(multiplexer_7_out[3:2]), .in_1(multiplexer_7_out[1:0]), .out(multiplexer_8_out));
  not not_2 (nor_2_out[0], multiplexer_8_out[0]);
  Multiplexer #(.Bits(32)) multiplexer_9 (
    .sel(nor_1_out), .in_0({nor_2_out, {27{1'b0}}}), .in_1({32{1'b1}}), .out(multiplexer_9_out));
  Multiplexer #(.Selector_Bits(4), .Bits(32)) multiplexer_10 (
    .sel(ALU_Ctrl[3:0]), .in_0(add_1_s), .in_1(sub_1_s), .in_2(mul_1_mul[31:0]), .in_3(multiplexer_2_out),
    .in_4(multiplexer_3_out), .in_5(and_3_out), .in_6(or_1_out), .in_7(xor_4_out), .in_8(not_1_out),
    .in_9({{26{1'b0}}, sub_2_s}), .in_10(multiplexer_9_out), .in_11({32{1'b0}}), .in_12({32{1'b0}}),
    .in_13({32{1'b0}}), .in_14({32{1'b0}}), .in_15({32{1'b0}}), .out({N, Result[30:0]}));
  Comparator #(.Bits(32)) comparator_2 (.a({N, Result[30:0]}), .b({32{1'b0}}), .eq(Z));  // open: gt, lt

  assign Result[31] = N;

  // Notes on the sheet:
  //   A: Operand 1
  //   B: Operand 2
  //   ALU_Ctrl: operation
  //   Result: Output
  //   Z: Zero?
  //   N: Negative? (sign bit)
  //   C: Carry? Result > 2^32 or < 0
  //   V: Overflow? Signed result is too large/small for destination
endmodule

/* Test case Test Data:
ALU_Ctrl A B Result Z N C V

# --- ADD ---
0x0  0x00000000  0x00000000  0x00000000  1 0 0 0
0x0  0xFFFFFFFF  0x00000001  0x00000000  1 0 1 0
0x0  0x7FFFFFFF  0x00000001  0x80000000  0 1 0 1
0x0  0x80000000  0x80000000  0x00000000  1 0 1 1
0x0  0xAAAAAAAA  0x55555555  0xFFFFFFFF  0 1 0 0
0x0  0xFFFFFFFF  0x00080004  0x00080003  0 0 1 0
0x0  0x12345678  0x00000000  0x12345678  0 0 0 0
0x0  0x4993B221  0x45FE9AB0  0x8F924CD1  0 1 0 1
0x0  0x44390BEC  0xC7D2EB07  0x0C0BF6F3  0 0 1 0
0x0  0xC1196DE2  0xF5F8F7E9  0xB71265CB  0 1 1 0
0x0  0x78EA231F  0x4E9EFFE0  0xC78922FF  0 1 0 1
0x0  0x67750BAF  0x221AFF67  0x89900B16  0 1 0 1
0x0  0xF7D709F6  0x5D70515B  0x55475B51  0 0 1 0
0x0  0xAD9E01B4  0x6D9459A0  0x1B325B54  0 0 1 0
0x0  0x4CEA40EB  0xDBE74473  0x28D1855E  0 0 1 0
0x0  0xFD0A4237  0x372E70C9  0x3438B300  0 0 1 0
0x0  0xB7E9469E  0x724E9153  0x2A37D7F1  0 0 1 0
0x0  0xEA00F62F  0x13857B50  0xFD86717F  0 1 0 0
0x0  0xA8BD1634  0x8E5E84D2  0x371B9B06  0 0 1 1
0x0  0xDE684DBF  0x7215F3FE  0x507E41BD  0 0 1 0
0x0  0xD6FC8FAC  0x367E651F  0x0D7AF4CB  0 0 1 0
0x0  0x843BDEB4  0x1006DD5C  0x9442BC10  0 1 0 0
0x0  0xBFB3C62F  0xA0DEED09  0x6092B338  0 0 1 1
0x0  0x547D8171  0x3D547A5F  0x91D1FBD0  0 1 0 1
0x0  0x2EADE470  0x040E2195  0x32BC0605  0 0 0 0
0x0  0x25A9C565  0x31A0BB94  0x574A80F9  0 0 0 0
0x0  0xB71A1134  0xDF241EBE  0x963E2FF2  0 1 1 0

# --- SUB ---
0x1  0x00000000  0x00000000  0x00000000  1 0 0 0
0x1  0xFFFFFFFF  0x00000001  0xFFFFFFFE  0 1 0 0
0x1  0x7FFFFFFF  0x00000001  0x7FFFFFFE  0 0 0 0
0x1  0x80000000  0x80000000  0x00000000  1 0 0 0
0x1  0xAAAAAAAA  0x55555555  0x55555555  0 0 0 1
0x1  0xFFFFFFFF  0x00080004  0xFFF7FFFB  0 1 0 0
0x1  0x12345678  0x00000000  0x12345678  0 0 0 0
0x1  0x4993B221  0x45FE9AB0  0x03951771  0 0 0 0
0x1  0x44390BEC  0xC7D2EB07  0x7C6620E5  0 0 1 0
0x1  0xC1196DE2  0xF5F8F7E9  0xCB2075F9  0 1 1 0
0x1  0x78EA231F  0x4E9EFFE0  0x2A4B233F  0 0 0 0
0x1  0x67750BAF  0x221AFF67  0x455A0C48  0 0 0 0
0x1  0xF7D709F6  0x5D70515B  0x9A66B89B  0 1 0 0
0x1  0xAD9E01B4  0x6D9459A0  0x4009A814  0 0 0 1
0x1  0x4CEA40EB  0xDBE74473  0x7102FC78  0 0 1 0
0x1  0xFD0A4237  0x372E70C9  0xC5DBD16E  0 1 0 0
0x1  0xB7E9469E  0x724E9153  0x459AB54B  0 0 0 1
0x1  0xEA00F62F  0x13857B50  0xD67B7ADF  0 1 0 0
0x1  0xA8BD1634  0x8E5E84D2  0x1A5E9162  0 0 0 0
0x1  0xDE684DBF  0x7215F3FE  0x6C5259C1  0 0 0 1
0x1  0xD6FC8FAC  0x367E651F  0xA07E2A8D  0 1 0 0
0x1  0x843BDEB4  0x1006DD5C  0x74350158  0 0 0 1
0x1  0xBFB3C62F  0xA0DEED09  0x1ED4D926  0 0 0 0
0x1  0x547D8171  0x3D547A5F  0x17290712  0 0 0 0
0x1  0x2EADE470  0x040E2195  0x2A9FC2DB  0 0 0 0
0x1  0x25A9C565  0x31A0BB94  0xF40909D1  0 1 1 0
0x1  0xB71A1134  0xDF241EBE  0xD7F5F276  0 1 1 0

# --- MUL ---
0x2  0x00000000  0x00000000  0x00000000  1 0 0 0
0x2  0xFFFFFFFF  0x00000001  0xFFFFFFFF  0 1 0 0
0x2  0x7FFFFFFF  0x00000001  0x7FFFFFFF  0 0 0 0
0x2  0x80000000  0x80000000  0x00000000  1 0 0 0
0x2  0xAAAAAAAA  0x55555555  0x71C71C72  0 0 0 0
0x2  0xFFFFFFFF  0x00080004  0xFFF7FFFC  0 1 0 0
0x2  0x12345678  0x00000000  0x00000000  1 0 0 0
0x2  0x4993B221  0x45FE9AB0  0x107050B0  0 0 0 0
0x2  0x44390BEC  0xC7D2EB07  0x7718F774  0 0 0 0
0x2  0xC1196DE2  0xF5F8F7E9  0x061A10B2  0 0 0 0
0x2  0x78EA231F  0x4E9EFFE0  0x24FC9C20  0 0 0 0
0x2  0x67750BAF  0x221AFF67  0xA4810469  0 1 0 0
0x2  0xF7D709F6  0x5D70515B  0xDD376072  0 1 0 0
0x2  0xAD9E01B4  0x6D9459A0  0x1168A480  0 0 0 0
0x2  0x4CEA40EB  0xDBE74473  0x63869591  0 0 0 0
0x2  0xFD0A4237  0x372E70C9  0xE0E80D2F  0 1 0 0
0x2  0xB7E9469E  0x724E9153  0xA1C5633A  0 1 0 0
0x2  0xEA00F62F  0x13857B50  0xFA0083B0  0 1 0 0
0x2  0xA8BD1634  0x8E5E84D2  0xE9A706A8  0 1 0 0
0x2  0xDE684DBF  0x7215F3FE  0x1BF47082  0 0 0 0
0x2  0xD6FC8FAC  0x367E651F  0xABEC41D4  0 1 0 0
0x2  0x843BDEB4  0x1006DD5C  0xACFD6CB0  0 1 0 0
0x2  0xBFB3C62F  0xA0DEED09  0x688D7AA7  0 0 0 0
0x2  0x547D8171  0x3D547A5F  0x9056E2EF  0 1 0 0
0x2  0x2EADE470  0x040E2195  0xD3C86530  0 1 0 0
0x2  0x25A9C565  0x31A0BB94  0x7D76E564  0 0 0 0
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*/
