// Digital circuit BranchHandler.dig as structural Verilog
module BranchHandler (
  input  [4:0] funct,
  input  Z,
  input  N,
  input  C,
  input  V,
  output JMP
);

  wire not_1_out, not_2_out, not_3_out, not_4_out, not_5_out, or_1_out, xor_1_out;

  not not_1 (not_1_out, Z);
  xor xor_1 (xor_1_out, N, V);
  not not_2 (not_2_out, C);
  not not_3 (not_3_out, N);
  or or_1 (or_1_out, xor_1_out, Z);
  not not_4 (not_4_out, or_1_out);
  not not_5 (not_5_out, xor_1_out);
  Multiplexer #(.Selector_Bits(4)) multiplexer_1 (
    .sel(funct[3:0]), .in_0(1'b1), .in_1(Z), .in_2(not_1_out), .in_3(xor_1_out), .in_4(or_1_out),
    .in_5(not_4_out), .in_6(not_5_out), .in_7(C), .in_8(not_2_out), .in_9(N), .in_10(not_3_out),
    .in_11(1'b0), .in_12(1'b0), .in_13(1'b0), .in_14(1'b0), .in_15(1'b0), .out(JMP));

  // Notes on the sheet:
  //   JMP: 1 if condition is met
endmodule
