// Digital circuit CPU.dig as structural Verilog
module CPU (
  input  clk
);

  wire and_1_out, branchhandler_1_jmp, cu_1_alumath, cu_1_branch, cu_1_fs, cu_1_immrs1, cu_1_immrs2,
       cu_1_jmpr, cu_1_load, cu_1_store, or_1_out;
  wire [1:0] cu_1_st;
  wire [3:0] alu_1_z, register_1_q;
  wire [4:0] cu_1_operation, cu_1_rd, cu_1_rs1, cu_1_rs1a, cu_1_rs2, cu_1_rs2b, multiplexer_2_out,
       multiplexer_3_out, multiplexer_4_out;
  wire [5:0] cu_1_sa;
  wire [12:0] cu_1_rs1immval, cu_1_rs2immval;
  wire [17:0] cu_1_offset;
  wire [31:0] add_1_s, add_2_s, alu_1_result, ifu_1_instr, ifu_1_pc, multiplexer_1_out, multiplexer_5_out,
       multiplexer_6_out, multiplexer_7_out, multiplexer_8_out, multiplexer_9_out, registerfile_1_rs1_data,
       registerfile_1_rs2_data, SLL_out, SRA_out, SRL_out;

  and and_1 (and_1_out, branchhandler_1_jmp, cu_1_branch);
  IFU ifu_1 (.clk(clk), .PC_Target(add_1_s), .PC_Src(and_1_out), .PC(ifu_1_pc), .Instr(ifu_1_instr));
  Add #(.Bits(32)) add_1 (.a(ifu_1_pc), .b(multiplexer_1_out), .c_i(1'b0), .s(add_1_s));  // open: c_o
  Multiplexer #(.Bits(32)) multiplexer_1 (
    .sel(cu_1_jmpr), .in_0({{14{1'b0}}, cu_1_offset}), .in_1(registerfile_1_rs1_data), .out(multiplexer_1_out));
  CU cu_1 (
    .Instruction(ifu_1_instr), .Rd(cu_1_rd), .Rs1(cu_1_rs1), .Rs2(cu_1_rs2), .ST(cu_1_st), .SA(cu_1_sa),
    .FS(cu_1_fs), .Rs1ImmVal(cu_1_rs1immval), .Offset(cu_1_offset), .Rs2ImmVal(cu_1_rs2immval),
    .Rs1A(cu_1_rs1a), .Rs2B(cu_1_rs2b), .ImmRs2(cu_1_immrs2), .ImmRs1(cu_1_immrs1),
    .operation(cu_1_operation), .ALUMath(cu_1_alumath), .Branch(cu_1_branch), .Load(cu_1_load),
    .Store(cu_1_store), .JMPR(cu_1_jmpr));  // open: Opcode
  Multiplexer #(.Bits(5)) multiplexer_2 (.sel(cu_1_immrs1), .in_0(cu_1_rs2), .in_1(cu_1_rs2b), .out(multiplexer_2_out));
  Multiplexer #(.Bits(5)) multiplexer_3 (.sel(cu_1_immrs2), .in_0(cu_1_rs1), .in_1(cu_1_rs1a), .out(multiplexer_3_out));
  Multiplexer #(.Bits(5)) multiplexer_4 (
    .sel(cu_1_store), .in_0(multiplexer_2_out), .in_1(cu_1_rd), .out(multiplexer_4_out));
  BranchHandler branchhandler_1 (
    .funct(cu_1_operation), .Z(register_1_q[0]), .N(register_1_q[1]), .C(register_1_q[2]),
    .V(register_1_q[3]), .JMP(branchhandler_1_jmp));
  Register #(.Bits(4)) register_1 (.D(alu_1_z), .C(clk), .en(cu_1_fs), .Q(register_1_q));
  or or_1 (or_1_out, cu_1_immrs2, cu_1_immrs1);
  RAMDualPort #(.AddrBits(24), .Bits(32)) ramdualport_1 (
    .A(add_2_s[23:0]), .Din(registerfile_1_rs2_data), .str(cu_1_store), .C(clk), .ld(cu_1_load));  // open: D
  Add #(.Bits(32)) add_2 (
    .a({{19{1'b0}}, cu_1_rs2immval}), .b(registerfile_1_rs1_data), .c_i(1'b0), .s(add_2_s));  // open: c_o
  Multiplexer #(.Bits(32)) multiplexer_5 (
    .sel(cu_1_immrs1), .in_0(registerfile_1_rs1_data), .in_1({{19{1'b0}}, cu_1_rs1immval}),
    .out(multiplexer_5_out));
  RegisterFile registerfile_1 (
    .Rs1(multiplexer_3_out), .Rs2(multiplexer_4_out), .Rd(cu_1_rd), .WD(multiplexer_9_out),
    .WE(cu_1_alumath), .Clk(clk), .Rs1_Data(registerfile_1_rs1_data), .Rs2_Data(registerfile_1_rs2_data));
  Multiplexer #(.Bits(32)) multiplexer_6 (
    .sel(cu_1_immrs2), .in_0(registerfile_1_rs2_data), .in_1({{19{1'b0}}, cu_1_rs2immval}),
    .out(multiplexer_6_out));
  ALU alu_1 (
    .A(multiplexer_5_out), .B(multiplexer_6_out), .ALU_Ctrl(cu_1_operation), .Result(alu_1_result),
    .Z(alu_1_z[0]), .N(alu_1_z[1]), .C(alu_1_z[2]), .V(alu_1_z[3]));
  BarrelShifter #(.Bits(32)) SLL (.in(alu_1_result), .shift(cu_1_sa), .out(SLL_out));
  BarrelShifter #(.Bits(32), .direction("right")) SRL (.in(alu_1_result), .shift(cu_1_sa), .out(SRL_out));
  Multiplexer #(.Selector_Bits(2), .Bits(32)) multiplexer_7 (
    .sel(cu_1_st), .in_0(SRA_out), .in_1(SRL_out), .in_2(SLL_out), .in_3({32{1'b0}}), .out(multiplexer_7_out));
  Multiplexer #(.Bits(32)) multiplexer_8 (
    .sel(or_1_out), .in_0(multiplexer_7_out), .in_1(alu_1_result), .out(multiplexer_8_out));
  Multiplexer #(.Bits(32)) multiplexer_9 (
    .sel(cu_1_jmpr), .in_0(multiplexer_8_out), .in_1(ifu_1_pc), .out(multiplexer_9_out));
  BarrelShifter #(.barrelShifterMode("arithmetic"), .Bits(32), .direction("right")) SRA (
    .in(alu_1_result), .shift(cu_1_sa), .out(SRA_out));
endmodule
