// Digital circuit CU.dig as structural Verilog
module CU (
  input  [31:0] Instruction,
  output [8:0] Opcode,
  output [4:0] Rd,
  output [4:0] Rs1,
  output [4:0] Rs2,
  output [1:0] ST,
  output [5:0] SA,
  output FS,
  output [12:0] Rs1ImmVal,
  output [17:0] Offset,
  output [12:0] Rs2ImmVal,
  output [4:0] Rs1A,
  output [4:0] Rs2B,
  output ImmRs2,
  output ImmRs1,
  output [4:0] operation,
  output ALUMath,
  output Branch,
  output Load,
  output Store,
  output JMPR
);

  wire demultiplexer_1_out_2;

  Demultiplexer #(.Selector_Bits(2)) demultiplexer_1 (
    .sel(Instruction[31:30]), .in(1'b1), .out_0(ALUMath), .out_1(Branch), .out_2(demultiplexer_1_out_2));  // open: out_3
  and and_1 (Load, demultiplexer_1_out_2, Instruction[29]);
  and and_2 (Store, demultiplexer_1_out_2, ~Instruction[29]);  // And
  and and_3 (JMPR, demultiplexer_1_out_2, Instruction[29]);

  assign FS = Instruction[0];
  assign ImmRs1 = Instruction[24];
  assign ImmRs2 = Instruction[23];
  assign Offset = Instruction[17:0];
  assign Opcode = Instruction[31:23];
  assign operation = Instruction[29:25];
  assign Rd = Instruction[22:18];
  assign Rs1 = Instruction[17:13];
  assign Rs1A = Instruction[17:13];
  assign Rs1ImmVal = Instruction[17:5];
  assign Rs2 = Instruction[12:8];
  assign Rs2B = Instruction[4:0];
  assign Rs2ImmVal = Instruction[12:0];
  assign SA = {1'b0, Instruction[5:1]};
  assign ST = Instruction[7:6];

  // Notes on the sheet:
  //   ST: Shift Type
  //   00: Logical Shift Left (LSL)
  //   01: Logical Shift Right (LSR)
  //   10: Arithmetic Shift Right (ASR)
  //   11: Reserved
  //   SA: Shift Amount
  //   FS: Freeze Status
  //   Rs1ImmVal: Freeze Status
  //   Rs2ImmVal: Freeze Status
  //   ImmRs2: Is Rs1 immediate?
  //   ImmRs1: Is Rs2 immediate?
  //   operation: Is Rs2 immediate?
  //   JMPR: Register-based jump
endmodule
