// Digital circuit IFU.dig as structural Verilog
module IFU (
  input  clk,
  input  [31:0] PC_Target,
  input  PC_Src,
  output [31:0] PC,
  output [31:0] Instr
);

  wire [31:0] add_1_s, multiplexer_1_out;

  Multiplexer #(.Bits(32)) multiplexer_1 (.sel(PC_Src), .in_0(add_1_s), .in_1(PC_Target), .out(multiplexer_1_out));
  Add #(.Bits(32)) add_1 (.a(PC), .b(32'h4), .c_i(1'b0), .s(add_1_s));  // open: c_o
  Register #(.Bits(32)) u_PC (.D(multiplexer_1_out), .C(clk), .en(1'b1), .Q(PC));
  ROM #(.AddrBits(10), .isProgramMemory("true"), .Bits(32)) Program (.A(PC[11:2]), .sel(1'b1), .D(Instr));

  // Notes on the sheet:
  //   clk: clock
  //   PC_Target: Instruction to JMP to
  //   PC_Src: If 0, the PC becomes PC + 4 . If 1, it accepts the PCSrc jump.
  //   PC: Current PC
  //   Instr: Instruction
  //   Program loads program.hex
endmodule

/* Test case:
clk PC_Src PC_Target   PC  Instr

# 1. Initialization: At startup, PC should be 0, reading the first line of code.
0   0     0          0   0x11111111

# 2. Normal Step: Clock ticks. PC should jump to 4, reading the second line.
c   0     0          4   0x22222222

# 3. Normal Step: Clock ticks again. PC should jump to 8, reading the third line.
c   0     0          8   0x33333333

# 4. The Branch Test: We flip the PCSrc multiplexer and tell it to jump to address 16.
c   1     16         16  0x55555555

# 5. Branch Recovery: We turn the MUX back to normal (0). It should resume counting by 4s from its new location (16 + 4 = 20).
c   0     0          20  0x66666666
*/
