// Digital circuit RegisterFile.dig as structural Verilog
module RegisterFile (
  input  [4:0] Rs1,
  input  [4:0] Rs2,
  input  [4:0] Rd,
  input  [31:0] WD,
  input  WE,
  input  Clk,
  output [31:0] Rs1_Data,
  output [31:0] Rs2_Data
);

  wire demultiplexer_1_out_1, demultiplexer_1_out_2, demultiplexer_1_out_3, demultiplexer_1_out_4,
       demultiplexer_1_out_5, demultiplexer_1_out_6, demultiplexer_1_out_7, demultiplexer_1_out_8,
       demultiplexer_1_out_9, demultiplexer_1_out_10, demultiplexer_1_out_11, demultiplexer_1_out_12,
       demultiplexer_1_out_13, demultiplexer_1_out_14, demultiplexer_1_out_15, demultiplexer_1_out_16,
       demultiplexer_1_out_17, demultiplexer_1_out_18, demultiplexer_1_out_19, demultiplexer_1_out_20,
       demultiplexer_1_out_21, demultiplexer_1_out_22, demultiplexer_1_out_23, demultiplexer_1_out_24,
       demultiplexer_1_out_25, demultiplexer_1_out_26, demultiplexer_1_out_27, demultiplexer_1_out_28,
       demultiplexer_1_out_29, demultiplexer_1_out_30, demultiplexer_1_out_31;
  wire [31:0] x1_q, x2_q, x3_q, x4_q, x5_q, x6_q, x7_q, x8_q, x9_q, x10_q, x11_q, x12_q, x13_q, x14_q, x15_q,
       x16_q, x17_q, x18_q, x19_q, x20_q, x21_q, x22_q, x23_q, x24_q, x25_q, x26_q, x27_q, x28_q, x29_q,
       x30_q, x31_q;

  // Probe Reg1 on WD
  Register #(.Bits(32)) x1 (.D(WD), .C(Clk), .en(demultiplexer_1_out_1), .Q(x1_q));
  Register #(.Bits(32)) x2 (.D(WD), .C(Clk), .en(demultiplexer_1_out_2), .Q(x2_q));
  Register #(.Bits(32)) x3 (.D(WD), .C(Clk), .en(demultiplexer_1_out_3), .Q(x3_q));
  Register #(.Bits(32)) x4 (.D(WD), .C(Clk), .en(demultiplexer_1_out_4), .Q(x4_q));
  Register #(.Bits(32)) x5 (.D(WD), .C(Clk), .en(demultiplexer_1_out_5), .Q(x5_q));
  Register #(.Bits(32)) x6 (.D(WD), .C(Clk), .en(demultiplexer_1_out_6), .Q(x6_q));
  Register #(.Bits(32)) x7 (.D(WD), .C(Clk), .en(demultiplexer_1_out_7), .Q(x7_q));
  Multiplexer #(.Selector_Bits(5), .Bits(32)) multiplexer_1 (
    .sel(Rs1), .in_0({32{1'b0}}), .in_1(x1_q), .in_2(x2_q), .in_3(x3_q), .in_4(x4_q), .in_5(x5_q),
    .in_6(x6_q), .in_7(x7_q), .in_8(x8_q), .in_9(x9_q), .in_10(x10_q), .in_11(x11_q), .in_12(x12_q),
    .in_13(x13_q), .in_14(x14_q), .in_15(x15_q), .in_16(x16_q), .in_17(x17_q), .in_18(x18_q), .in_19(x19_q),
    .in_20(x20_q), .in_21(x21_q), .in_22(x22_q), .in_23(x23_q), .in_24(x24_q), .in_25(x25_q), .in_26(x26_q),
    .in_27(x27_q), .in_28(x28_q), .in_29(x29_q), .in_30(x30_q), .in_31(x31_q), .out(Rs1_Data));
  Demultiplexer #(.Selector_Bits(5)) demultiplexer_1 (
    .sel(Rd), .in(WE), .out_1(demultiplexer_1_out_1), .out_2(demultiplexer_1_out_2),
    .out_3(demultiplexer_1_out_3), .out_4(demultiplexer_1_out_4), .out_5(demultiplexer_1_out_5),
    .out_6(demultiplexer_1_out_6), .out_7(demultiplexer_1_out_7), .out_8(demultiplexer_1_out_8),
    .out_9(demultiplexer_1_out_9), .out_10(demultiplexer_1_out_10), .out_11(demultiplexer_1_out_11),
    .out_12(demultiplexer_1_out_12), .out_13(demultiplexer_1_out_13), .out_14(demultiplexer_1_out_14),
    .out_15(demultiplexer_1_out_15), .out_16(demultiplexer_1_out_16), .out_17(demultiplexer_1_out_17),
    .out_18(demultiplexer_1_out_18), .out_19(demultiplexer_1_out_19), .out_20(demultiplexer_1_out_20),
    .out_21(demultiplexer_1_out_21), .out_22(demultiplexer_1_out_22), .out_23(demultiplexer_1_out_23),
    .out_24(demultiplexer_1_out_24), .out_25(demultiplexer_1_out_25), .out_26(demultiplexer_1_out_26),
    .out_27(demultiplexer_1_out_27), .out_28(demultiplexer_1_out_28), .out_29(demultiplexer_1_out_29),
    .out_30(demultiplexer_1_out_30), .out_31(demultiplexer_1_out_31));  // open: out_0
  Register #(.Bits(32)) x8 (.D(WD), .C(Clk), .en(demultiplexer_1_out_8), .Q(x8_q));
  Register #(.Bits(32)) x9 (.D(WD), .C(Clk), .en(demultiplexer_1_out_9), .Q(x9_q));
  Register #(.Bits(32)) x10 (.D(WD), .C(Clk), .en(demultiplexer_1_out_10), .Q(x10_q));
  Register #(.Bits(32)) x11 (.D(WD), .C(Clk), .en(demultiplexer_1_out_11), .Q(x11_q));
  Register #(.Bits(32)) x12 (.D(WD), .C(Clk), .en(demultiplexer_1_out_12), .Q(x12_q));
  Register #(.Bits(32)) x13 (.D(WD), .C(Clk), .en(demultiplexer_1_out_13), .Q(x13_q));
  Register #(.Bits(32)) x14 (.D(WD), .C(Clk), .en(demultiplexer_1_out_14), .Q(x14_q));
  Register #(.Bits(32)) x15 (.D(WD), .C(Clk), .en(demultiplexer_1_out_15), .Q(x15_q));
  Register #(.Bits(32)) x16 (.D(WD), .C(Clk), .en(demultiplexer_1_out_16), .Q(x16_q));
  Register #(.Bits(32)) x17 (.D(WD), .C(Clk), .en(demultiplexer_1_out_17), .Q(x17_q));
  Register #(.Bits(32)) x18 (.D(WD), .C(Clk), .en(demultiplexer_1_out_18), .Q(x18_q));
  Register #(.Bits(32)) x19 (.D(WD), .C(Clk), .en(demultiplexer_1_out_19), .Q(x19_q));
  Register #(.Bits(32)) x20 (.D(WD), .C(Clk), .en(demultiplexer_1_out_20), .Q(x20_q));
  Register #(.Bits(32)) x21 (.D(WD), .C(Clk), .en(demultiplexer_1_out_21), .Q(x21_q));
  Register #(.Bits(32)) x22 (.D(WD), .C(Clk), .en(demultiplexer_1_out_22), .Q(x22_q));
  Register #(.Bits(32)) x23 (.D(WD), .C(Clk), .en(demultiplexer_1_out_23), .Q(x23_q));
  Multiplexer #(.Selector_Bits(5), .Bits(32)) multiplexer_2 (
    .sel(Rs2), .in_0({32{1'b0}}), .in_1(x1_q), .in_2(x2_q), .in_3(x3_q), .in_4(x4_q), .in_5(x5_q),
    .in_6(x6_q), .in_7(x7_q), .in_8(x8_q), .in_9(x9_q), .in_10(x10_q), .in_11(x11_q), .in_12(x12_q),
    .in_13(x13_q), .in_14(x14_q), .in_15(x15_q), .in_16(x16_q), .in_17(x17_q), .in_18(x18_q), .in_19(x19_q),
    .in_20(x20_q), .in_21(x21_q), .in_22(x22_q), .in_23(x23_q), .in_24(x24_q), .in_25(x25_q), .in_26(x26_q),
    .in_27(x27_q), .in_28(x28_q), .in_29(x29_q), .in_30(x30_q), .in_31(x31_q), .out(Rs2_Data));
  Register #(.Bits(32)) x24 (.D(WD), .C(Clk), .en(demultiplexer_1_out_24), .Q(x24_q));
  Register #(.Bits(32)) x25 (.D(WD), .C(Clk), .en(demultiplexer_1_out_25), .Q(x25_q));
  Register #(.Bits(32)) x26 (.D(WD), .C(Clk), .en(demultiplexer_1_out_26), .Q(x26_q));
  Register #(.Bits(32)) x27 (.D(WD), .C(Clk), .en(demultiplexer_1_out_27), .Q(x27_q));
  Register #(.Bits(32)) x28 (.D(WD), .C(Clk), .en(demultiplexer_1_out_28), .Q(x28_q));
  Register #(.Bits(32)) x29 (.D(WD), .C(Clk), .en(demultiplexer_1_out_29), .Q(x29_q));
  Register #(.Bits(32)) x30 (.D(WD), .C(Clk), .en(demultiplexer_1_out_30), .Q(x30_q));
  Register #(.Bits(32)) x31 (.D(WD), .C(Clk), .en(demultiplexer_1_out_31), .Q(x31_q));

  // Notes on the sheet:
  //   Rs1: Address for Source Register 1
  //   Rs2: Address for Source Register 2
  //   Rd: Address for the Destination Register
  //   WD: Value to write to Rd
  //   WE: If 1, CPU can write data to Rd. If 0, Write_Data is ignored
  //   Clk: Clock
  //   Rs1_Data: Data in Rs1
  //   Rs2_Data: Data in Rs2
endmodule

/* Test case:
Clk WE Rd WD Rs1 Rs2 Rs1_Data Rs2_Data

# 1. Start empty. Read x0. It MUST be 0.
0 0  0  0x00000000  0   0   0x00000000  0x00000000

# 2. The Golden Rule Test: Try to overwrite x0
# We attempt to write FFFFFFFF to x0, but x0 must ignore it.
c 1  0  0xFFFFFFFF  0   0   0x00000000  0x00000000

# 3. Basic Write & Read
# Write 11111111 to x1. Read it on Rs1.
c 1  1  0x11111111  1   0   0x11111111  0x00000000

# 4. Dual-Port Independence
# Write 22222222 to x2. Read x1 on Rs1, and x2 on Rs2 simultaneously.
c 1  2  0x22222222  1   2   0x11111111  0x22222222

# 5. The Write-Enable (WE) Security Test
# Try to write 33333333 to x3, but leave WE = 0. It should NOT save.
c 0  3  0x33333333  3   2   0x00000000  0x22222222
# Now turn WE = 1. It SHOULD save.
c 1  3  0x33333333  3   2   0x33333333  0x22222222

# 6. The Extremes (Test the top register x31)
c 1  31 0xDEADBEEF  31  3   0xDEADBEEF  0x33333333
*/
